// Logisim project cod.circ as structural Verilog
module Q1A_AND_gate (
  input  A,
  input  B,
  output C
);

  and and_1 (C, A, B);
endmodule

module Q1b_NOT_gate (
  output A,
  output B
);

  not not_1 (B, A);
endmodule

module Q1c_Or_gate (
  input  A,
  input  B,
  output C
);

  or or_1 (C, A, B);
endmodule

module Q1d_OR_gate (
  input  A,
  input  B,
  output C
);

  nor nor_1 (C, A, B);
endmodule

module Q1e_nand_gate (
  input  in_1,
  input  in_2,
  output out_3
);

  nand nand_1 (out_3, in_1, in_2);
endmodule

module Q1f_ex_or_gate (
  input  in_1,
  input  in_2,
  output out_3
);

  xor xor_1 (out_3, in_1, in_2);
endmodule

module Q1g_xnor_gate (
  input  in_1,
  input  in_2,
  output out_3
);

  xnor xnor_1 (out_3, in_1, in_2);
endmodule

module Q2_a (
  input  in_1,
  input  in_2,
  output out_3
);

  wire nand_1_out;

  nand nand_1 (nand_1_out, in_1, in_2);
  not not_1 (out_3, nand_1_out);
endmodule

module Q2b (
  input  in_1,
  input  in_2,
  output out_3
);

  wire nand_1_out;

  nand nand_1 (nand_1_out, in_1, in_2);
  and and_1 (out_3, nand_1_out, nand_1_out);
endmodule

module Q2_c (
  input  in_1,
  input  in_2,
  output out_3
);

  wire nand_1_out, nand_2_out;

  nand nand_1 (nand_1_out, in_1, in_1);
  nand nand_2 (nand_2_out, in_2, in_2);
  nand nand_3 (out_3, nand_1_out, nand_2_out);
endmodule

module Q3 (
  input  in_1,
  output out_2
);

  nor nor_1 (out_2, in_1, in_1);
endmodule

module Q4 (
  input  in_1,
  input  in_2,
  input  in_3,
  output out_4
);

  wire nand_1_out, not_1_out;

  not not_1 (not_1_out, in_3);
  nand nand_1 (nand_1_out, in_1, in_2);
  or or_1 (out_4, nand_1_out, not_1_out);
endmodule

module Q4_2 (
  input  in_1,
  input  in_2,
  input  in_3,
  output out_4
);

  wire and_1_out, nor_1_out;

  nor nor_1 (nor_1_out, in_1, in_2);
  and and_1 (and_1_out, in_2, in_3);
  or or_1 (out_4, nor_1_out, and_1_out);
endmodule

module Q5 (
  input  in_1,
  input  in_2,
  output out_3
);

  and and_1 (out_3, in_1, in_2);
endmodule

module Q5b (
  input  in_1,
  input  in_2,
  output out_3
);

  or or_1 (out_3, in_1, in_2);
endmodule

module Q6 (
  input  in_1,
  input  in_2,
  input  in_3,
  output out_4
);

  wire not_1_out, or_1_out;

  or or_1 (or_1_out, in_1, in_2);
  not not_1 (not_1_out, in_3);
  and and_1 (out_4, or_1_out, not_1_out);
endmodule

module Q7 (
  input  in_1,
  input  in_2,
  input  in_3,
  output out_4
);

  or or_1 (out_4, in_1, in_2, in_3);
endmodule

module Q8b (
  input  in_1,
  input  in_2,
  input  in_3,
  input  in_4,
  input  in_5,
  input  in_6,
  output out_7
);

  wire and_1_out, nand_1_out, nand_2_out;

  nand nand_1 (nand_1_out, in_1, in_2);
  and and_1 (and_1_out, in_3, in_4);
  nand nand_2 (nand_2_out, in_5, in_6);
  or or_1 (out_7, nand_1_out, and_1_out, nand_2_out);
endmodule

module Q8c (
  input  in_1,
  input  in_2,
  input  in_3,
  output out_4
);

  wire not_1_out, or_1_out, or_2_out, or_3_out;

  not not_1 (not_1_out, in_1);
  or or_1 (or_1_out, not_1_out, in_2);
  or or_2 (or_2_out, in_2, in_3);
  or or_3 (or_3_out, in_1, in_3);
  and and_1 (out_4, or_1_out, or_2_out, or_3_out);
endmodule
